// Logisim project prova_pc_revisione.circ as structural Verilog: 9 circuits, main circuit main
module main (
  output [3:0] out_1
);

  wire alu_1_negative, alu_1_zero, alu_en_q, clk, control_logic_1_alu_en, control_logic_1_alu_op,
       control_logic_1_alu_rs1_im, control_logic_1_block_fetch, control_logic_1_im_en, control_logic_1_jump,
       control_logic_1_load_en, control_logic_1_rd_en, control_logic_1_rs1_en, control_logic_1_rs2_en,
       control_logic_1_rst_en, controlled_buffer_1_out, controlled_buffer_2_out, load_en_1_q, load_en_2_q,
       load_en_q, not_1_out, not_3_out, not_4_out, not_5_out, op_q, rd_1_q, rd_2_q, rd_q, rgb_video_1_p1,
       rgb_video_1_p2, rs2_im_q, rst_en_1_q, rst_en_q, s_out, w_out;
  wire [2:0] rgb_video_1_p5;
  wire [3:0] control_logic_1_rd, control_logic_1_rs1, control_logic_1_rs2, control_logic_1_rst, rd_data_1_q,
       rd_data_q, rgb_video_1_p3, rgb_video_1_p4;
  wire [7:0] adder_8_bit_1_somma, alu_1_risultato, control_logic_1_im, control_logic_1_istr_addr,
       controlled_buffer_3_out, imm_q, multiplexer_1_out, multiplexer_2_out, ram_1_dout, register_1_q,
       register_file_1_data_out3, ris1_q, ris_q, rs1_q, rs2_q, rst_1_q, rst_q;
  wire [7:4] register_file_1_data_out1, register_file_1_data_out2;
  wire [15:0] rom_1_data;

  Multiplexer #(.width(8)) multiplexer_1 (
    .in0(adder_8_bit_1_somma), .in1(control_logic_1_istr_addr), .out(multiplexer_1_out),
    .sel(control_logic_1_jump));
  Clock clock_1 (.out(clk));
  // Probe on controlled_buffer_3_out
  Adder_8_Bit adder_8_bit_1 (.A(register_1_q), .B(8'h1), .Somma(adder_8_bit_1_somma));  // open: r, Resto
  assign controlled_buffer_1_out = not_1_out ? clk : 1'bz;  // Controlled_Buffer controlled_buffer_1
  not not_1 (not_1_out, control_logic_1_block_fetch);
  Register register_1 (
    .D(multiplexer_1_out), .en(controlled_buffer_1_out), .clk(controlled_buffer_1_out), .Q(register_1_q));  // open: clr
  ROM #(.dataWidth(16)) rom_1 (.addr(register_1_q), .data(rom_1_data));
  Button w (.out(w_out));
  Button s (.out(s_out));
  // NOT_Gate not_2 has open pins: in=clk, out=open
  // RGB_Video #(.cursor("No Cursor"), .height(16), .reset("Synchronous"), .scale(8), .width(16)) rgb_video_1: pin names not known; wires that end beside it: rgb_video_1_p1, rgb_video_1_p2, rgb_video_1_p3, rgb_video_1_p4, rgb_video_1_p5
  Control_logic control_logic_1 (
    .in_1(rom_1_data), .zero(alu_1_zero), .negative(alu_1_negative), .In_rd(rd_q), .In_rd_data(rd_data_q),
    .In_rd_1(rd_1_q), .In_rd_data_1(rd_data_1_q), .In_rd_2(rd_2_q), .In_rd_data_2(out_1),
    .istr_addr_in(register_1_q), .sf1(w_out), .sf2(s_out), .rd(control_logic_1_rd),
    .rd_en(control_logic_1_rd_en), .rs1(control_logic_1_rs1), .rs1_en(control_logic_1_rs1_en),
    .rs2(control_logic_1_rs2), .rs2_en(control_logic_1_rs2_en), .im(control_logic_1_im),
    .im_en(control_logic_1_im_en), .Alu_en(control_logic_1_alu_en), .Alu_op(control_logic_1_alu_op),
    .Alu_rs1_im(control_logic_1_alu_rs1_im), .Jump(control_logic_1_jump),
    .Istr_addr(control_logic_1_istr_addr), .Block_fetch(control_logic_1_block_fetch),
    .rst(control_logic_1_rst), .rst_en(control_logic_1_rst_en), .load_en(control_logic_1_load_en),
    .rgb(rgb_video_1_p5), .clr(rgb_video_1_p1), .screen_en(rgb_video_1_p2));  // open: sf3, sf4
  not not_3 (not_3_out, control_logic_1_block_fetch);
  // Probe on out_1
  // Probe on controlled_buffer_3_out
  not not_4 (not_4_out, clk);
  // Probe on {register_file_1_data_out2, rgb_video_1_p4}
  Register_File register_file_1 (
    .Data_In(controlled_buffer_3_out), .In_address(out_1), .In_enabled(rd_2_q),
    .Out1_address(control_logic_1_rs1), .Out2_address(control_logic_1_rs2),
    .Out3_address(control_logic_1_rst), .Clock(not_4_out),
    .Data_out1({register_file_1_data_out1, rgb_video_1_p3}),
    .Data_out2({register_file_1_data_out2, rgb_video_1_p4}), .Data_out3(register_file_1_data_out3));
  // Probe on {register_file_1_data_out1, rgb_video_1_p3}
  D_Flip_Flop rd (.D(control_logic_1_rd_en), .clk(clk), .Q(rd_q));  // open: Qn, preset, reset
  Register #(.width(4)) rd_data (
    .D(control_logic_1_rd), .en(control_logic_1_rd_en), .clk(controlled_buffer_2_out), .Q(rd_data_q));  // open: clr
  Register rs1 (
    .D({register_file_1_data_out1, rgb_video_1_p3}), .en(control_logic_1_rs1_en),
    .clk(controlled_buffer_2_out), .Q(rs1_q));  // open: clr
  Register rs2 (
    .D({register_file_1_data_out2, rgb_video_1_p4}), .en(control_logic_1_rs2_en),
    .clk(controlled_buffer_2_out), .Q(rs2_q));  // open: clr
  Register imm (
    .D(control_logic_1_im), .en(control_logic_1_im_en), .clk(controlled_buffer_2_out), .Q(imm_q));  // open: clr
  assign controlled_buffer_2_out = not_3_out ? clk : 1'bz;  // Controlled_Buffer controlled_buffer_2
  Register rst (
    .D(register_file_1_data_out3), .en(control_logic_1_rst_en), .clk(controlled_buffer_2_out), .Q(rst_q));  // open: clr
  D_Flip_Flop op (.D(control_logic_1_alu_op), .clk(controlled_buffer_2_out), .Q(op_q));  // open: Qn, preset, reset
  D_Flip_Flop rs2_im (
    .D(control_logic_1_alu_rs1_im), .clk(controlled_buffer_2_out), .Q(rs2_im_q));  // open: Qn, preset, reset
  D_Flip_Flop alu_en (
    .D(control_logic_1_alu_en), .clk(controlled_buffer_2_out), .Q(alu_en_q));  // open: Qn, preset, reset
  D_Flip_Flop rst_en (
    .D(control_logic_1_rst_en), .clk(controlled_buffer_2_out), .Q(rst_en_q));  // open: Qn, preset, reset
  D_Flip_Flop load_en (
    .D(control_logic_1_load_en), .clk(controlled_buffer_2_out), .Q(load_en_q));  // open: Qn, preset, reset
  Alu alu_1 (
    .A(rs1_q), .B(multiplexer_2_out), .Sum_Sub(op_q), .Risultato(alu_1_risultato), .Negative(alu_1_negative),
    .Zero(alu_1_zero));  // open: Overflow
  Multiplexer #(.width(8)) multiplexer_2 (.in0(rs2_q), .in1(imm_q), .out(multiplexer_2_out), .sel(rs2_im_q));
  D_Flip_Flop rd_1 (.D(rd_q), .clk(clk), .Q(rd_1_q));  // open: Qn, preset, reset
  Register #(.width(4)) rd_data_1 (.D(rd_data_q), .en(rd_q), .clk(clk), .Q(rd_data_1_q));  // open: clr
  Register ris (.D(alu_1_risultato), .en(alu_en_q), .clk(clk), .Q(ris_q));  // open: clr
  Register rst_1 (.D(rst_q), .en(rst_en_q), .clk(clk), .Q(rst_1_q));  // open: clr
  D_Flip_Flop rst_en_1 (.D(rst_en_q), .clk(clk), .Q(rst_en_1_q));  // open: Qn, preset, reset
  D_Flip_Flop load_en_1 (.D(load_en_q), .clk(clk), .Q(load_en_1_q));  // open: Qn, preset, reset
  RAM ram_1 (.addr(ris_q), .we(rst_en_1_q), .oe(load_en_1_q), .clk(clk), .din(rst_1_q), .dout(ram_1_dout));
  D_Flip_Flop rd_2 (.D(rd_1_q), .clk(clk), .Q(rd_2_q));  // open: Qn, preset, reset
  Register #(.width(4)) rd_data_2 (.D(rd_data_1_q), .en(rd_1_q), .clk(clk), .Q(out_1));  // open: clr
  Register ris1 (.D(ris_q), .en(clk), .clk(clk), .Q(ris1_q));  // open: clr
  assign controlled_buffer_3_out = not_5_out ? ris1_q : 8'bz;  // Controlled_Buffer controlled_buffer_3
  not not_5 (not_5_out, load_en_2_q);
  D_Flip_Flop load_en_2 (.D(load_en_1_q), .clk(clk), .Q(load_en_2_q));  // open: Qn, preset, reset
  assign controlled_buffer_3_out = load_en_2_q ? ram_1_dout : 8'bz;  // Controlled_Buffer controlled_buffer_4

  // Notes on the sheet:
  //   istruction fetch
  //   contents of rom_1 (hex, n*v repeats v):
  //   16b 88b fab f9b 8eb 5db 1cb ffbb 800c 505 28f3 289 3f9 e9 1d9 7dec 4774 4b84 fcf3 2414 1cf3 2b14
  //   fbf3 3914 1bf3 4014 17 127 21c 217 327 81f2 d14 16c 26c 904 9ef2 2854 cee1 1404 ffcb cee1 1604 eef3
  //   5624 eef3 3734 2813 1df2 3734 8df2 3724 1cb cee1 1604 cee1 1604 adf2 3d54 bdd1 1804 ffbb bdd1 1a04
  //   fdf3 4424 bdd1 1a04 1bb bdd1 1a04 f8f3 1224 f883 1204 28f3 aff2 1254 1883 1204 1813 2823 786c 716c
  //   726c 6 5604
  //   istruction decode
  //   execute
  //   memory acces
  //   write back
endmodule

// 1-reg
module Register_1_bit (
  input  Data,
  input  Enabled,
  input  Clock,
  input  Azzera,
  output Q
);

  wire and_1_out;

  D_Flip_Flop d_ff_1 (.D(Data), .clk(and_1_out), .Q(Q), .reset(Azzera));  // open: Qn, preset
  and and_1 (and_1_out, Enabled, Clock);
endmodule

// 8-Reg
module Register_8_Bit (
  input  [7:0] Data,
  input  Enabled,
  input  Clock,
  output [7:0] out_4
);

  wire and_1_out;

  and and_1 (and_1_out, Enabled, Clock);
  D_Flip_Flop d_ff_1 (.D(Data[0]), .clk(and_1_out), .Q(out_4[0]));  // open: Qn, preset, reset
  D_Flip_Flop d_ff_2 (.D(Data[1]), .clk(and_1_out), .Q(out_4[1]));  // open: Qn, preset, reset
  D_Flip_Flop d_ff_3 (.D(Data[2]), .clk(and_1_out), .Q(out_4[2]));  // open: Qn, preset, reset
  D_Flip_Flop d_ff_4 (.D(Data[3]), .clk(and_1_out), .Q(out_4[3]));  // open: Qn, preset, reset
  D_Flip_Flop d_ff_5 (.D(Data[4]), .clk(and_1_out), .Q(out_4[4]));  // open: Qn, preset, reset
  D_Flip_Flop d_ff_6 (.D(Data[5]), .clk(and_1_out), .Q(out_4[5]));  // open: Qn, preset, reset
  D_Flip_Flop d_ff_7 (.D(Data[6]), .clk(and_1_out), .Q(out_4[6]));  // open: Qn, preset, reset
  D_Flip_Flop d_ff_8 (.D(Data[7]), .clk(and_1_out), .Q(out_4[7]));  // open: Qn, preset, reset
endmodule

// F Ad
module Full_Adder (
  input  A,
  input  B,
  input  C,
  output Somma,
  output Resto
);

  wire half_adder_1_resto, half_adder_1_somma, half_adder_2_resto;

  Half_Adder half_adder_1 (.A(A), .B(B), .Resto(half_adder_1_resto), .Somma(half_adder_1_somma));
  Half_Adder half_adder_2 (.A(half_adder_1_somma), .B(C), .Resto(half_adder_2_resto), .Somma(Somma));
  or or_1 (Resto, half_adder_1_resto, half_adder_2_resto);
endmodule

// H-A
module Half_Adder (
  input  A,
  input  B,
  output Somma,
  output Resto
);

  and and_1 (Resto, B, A);
  xor xor_1 (Somma, A, B);
endmodule

// Ad 8b
module Adder_8_Bit (
  input  r,
  input  [7:0] A,
  input  [7:0] B,
  output [7:0] Somma,
  output Resto
);

  wire full_adder_1_resto, full_adder_2_resto, full_adder_3_resto, full_adder_4_resto, full_adder_5_resto,
       full_adder_6_resto, full_adder_7_resto;

  Full_Adder full_adder_1 (.B(A[0]), .C(B[0]), .A(r), .Resto(full_adder_1_resto), .Somma(Somma[0]));
  Full_Adder full_adder_2 (.B(A[1]), .C(B[1]), .A(full_adder_1_resto), .Resto(full_adder_2_resto), .Somma(Somma[1]));
  Full_Adder full_adder_3 (.B(A[2]), .C(B[2]), .A(full_adder_2_resto), .Resto(full_adder_3_resto), .Somma(Somma[2]));
  Full_Adder full_adder_4 (.B(A[3]), .C(B[3]), .A(full_adder_3_resto), .Resto(full_adder_4_resto), .Somma(Somma[3]));
  Full_Adder full_adder_5 (.B(A[4]), .C(B[4]), .A(full_adder_4_resto), .Resto(full_adder_5_resto), .Somma(Somma[4]));
  Full_Adder full_adder_6 (.B(A[5]), .C(B[5]), .A(full_adder_5_resto), .Resto(full_adder_6_resto), .Somma(Somma[5]));
  Full_Adder full_adder_7 (.B(A[6]), .C(B[6]), .A(full_adder_6_resto), .Resto(full_adder_7_resto), .Somma(Somma[6]));
  Full_Adder full_adder_8 (.B(A[7]), .C(B[7]), .A(full_adder_7_resto), .Resto(Resto), .Somma(Somma[7]));
endmodule

module Alu (
  input  Sum_Sub,
  input  [7:0] A,
  input  [7:0] B,
  output [7:0] Risultato,
  output Overflow,
  output Negative,
  output Zero
);

  wire and_1_out, and_2_out, and_3_out, and_4_out, not_1_out, not_2_out, or_2_out;
  wire [7:0] xor_1_out;

  and and_1 (and_1_out, ~B[7], ~A[7], ~Sum_Sub, Risultato[7]);  // AND_Gate
  assign xor_1_out = B ^ {8{Sum_Sub}};  // XOR_Gate xor_1, 8 bits wide
  and and_2 (and_2_out, B[7], A[7], ~Sum_Sub, ~Risultato[7]);  // AND_Gate
  Adder_8_Bit adder_8_bit_1 (.A(A), .B(xor_1_out), .r(Sum_Sub), .Somma(Risultato));  // open: Resto
  and and_3 (and_3_out, ~B[7], A[7], Sum_Sub, ~Risultato[7]);  // AND_Gate
  or or_1 (Overflow, and_1_out, and_2_out, and_3_out, and_4_out);
  and and_4 (and_4_out, B[7], ~A[7], Sum_Sub, Risultato[7]);  // AND_Gate
  not not_1 (not_1_out, Overflow);
  and and_5 (Negative, not_1_out, Risultato[7]);
  or or_2 (or_2_out, Risultato[7], Risultato[6], Risultato[5], Risultato[4], Risultato[3], Risultato[2], Risultato[1], Risultato[0]);
  not not_2 (not_2_out, or_2_out);
  and and_6 (Zero, not_1_out, not_2_out);
endmodule

module Register_File (
  input  [7:0] Data_In,
  input  [3:0] In_address,
  input  In_enabled,
  input  [3:0] Out1_address,
  input  [3:0] Out2_address,
  input  [3:0] Out3_address,
  input  Clock,
  output [7:0] Data_out1,
  output [7:0] Data_out2,
  output [7:0] Data_out3
);

  wire and_1_out, demultiplexer_1_out0, demultiplexer_1_out1, demultiplexer_1_out2, demultiplexer_1_out3,
       demultiplexer_1_out4, demultiplexer_1_out5, demultiplexer_1_out6, demultiplexer_1_out7,
       demultiplexer_1_out8, demultiplexer_1_out9, demultiplexer_1_out10, demultiplexer_1_out11,
       demultiplexer_1_out12, demultiplexer_1_out13, demultiplexer_1_out14, demultiplexer_1_out15;
  wire [7:0] register_8_bit_1_out_4, register_8_bit_2_out_4, register_8_bit_3_out_4, register_8_bit_4_out_4,
       register_8_bit_5_out_4, register_8_bit_6_out_4, register_8_bit_7_out_4, register_8_bit_8_out_4,
       register_8_bit_9_out_4, register_8_bit_10_out_4, register_8_bit_11_out_4, register_8_bit_12_out_4,
       register_8_bit_13_out_4, register_8_bit_14_out_4, register_8_bit_15_out_4, register_8_bit_16_out_4;

  and and_1 (and_1_out, 1'b1, In_enabled);
  Demultiplexer #(.select(4)) demultiplexer_1 (
    .out0(demultiplexer_1_out0), .out1(demultiplexer_1_out1), .out2(demultiplexer_1_out2),
    .out3(demultiplexer_1_out3), .out4(demultiplexer_1_out4), .out5(demultiplexer_1_out5),
    .out6(demultiplexer_1_out6), .out7(demultiplexer_1_out7), .out8(demultiplexer_1_out8),
    .out9(demultiplexer_1_out9), .out10(demultiplexer_1_out10), .out11(demultiplexer_1_out11),
    .out12(demultiplexer_1_out12), .out13(demultiplexer_1_out13), .out14(demultiplexer_1_out14),
    .out15(demultiplexer_1_out15), .in(and_1_out), .sel(In_address));
  Register_8_Bit register_8_bit_1 (
    .Data({8{1'b0}}), .Enabled(demultiplexer_1_out0), .Clock(Clock), .out_4(register_8_bit_1_out_4));
  Register_8_Bit register_8_bit_2 (
    .Data(Data_In), .Enabled(demultiplexer_1_out4), .Clock(Clock), .out_4(register_8_bit_2_out_4));
  Register_8_Bit register_8_bit_3 (
    .Data(Data_In), .Enabled(demultiplexer_1_out8), .Clock(Clock), .out_4(register_8_bit_3_out_4));
  Register_8_Bit register_8_bit_4 (
    .Data(Data_In), .Enabled(demultiplexer_1_out12), .Clock(Clock), .out_4(register_8_bit_4_out_4));
  Register_8_Bit register_8_bit_5 (
    .Data(Data_In), .Enabled(demultiplexer_1_out1), .Clock(Clock), .out_4(register_8_bit_5_out_4));
  Register_8_Bit register_8_bit_6 (
    .Data(Data_In), .Enabled(demultiplexer_1_out5), .Clock(Clock), .out_4(register_8_bit_6_out_4));
  Register_8_Bit register_8_bit_7 (
    .Data(Data_In), .Enabled(demultiplexer_1_out9), .Clock(Clock), .out_4(register_8_bit_7_out_4));
  Register_8_Bit register_8_bit_8 (
    .Data(Data_In), .Enabled(demultiplexer_1_out13), .Clock(Clock), .out_4(register_8_bit_8_out_4));
  Register_8_Bit register_8_bit_9 (
    .Data(Data_In), .Enabled(demultiplexer_1_out2), .Clock(Clock), .out_4(register_8_bit_9_out_4));
  Register_8_Bit register_8_bit_10 (
    .Data(Data_In), .Enabled(demultiplexer_1_out6), .Clock(Clock), .out_4(register_8_bit_10_out_4));
  Register_8_Bit register_8_bit_11 (
    .Data(Data_In), .Enabled(demultiplexer_1_out10), .Clock(Clock), .out_4(register_8_bit_11_out_4));
  Register_8_Bit register_8_bit_12 (
    .Data(Data_In), .Enabled(demultiplexer_1_out14), .Clock(Clock), .out_4(register_8_bit_12_out_4));
  Register_8_Bit register_8_bit_13 (
    .Data(Data_In), .Enabled(demultiplexer_1_out3), .Clock(Clock), .out_4(register_8_bit_13_out_4));
  Register_8_Bit register_8_bit_14 (
    .Data(Data_In), .Enabled(demultiplexer_1_out7), .Clock(Clock), .out_4(register_8_bit_14_out_4));
  Register_8_Bit register_8_bit_15 (
    .Data(Data_In), .Enabled(demultiplexer_1_out11), .Clock(Clock), .out_4(register_8_bit_15_out_4));
  Register_8_Bit register_8_bit_16 (
    .Data(Data_In), .Enabled(demultiplexer_1_out15), .Clock(Clock), .out_4(register_8_bit_16_out_4));
  Multiplexer #(.select(4), .width(8)) multiplexer_1 (
    .in0(register_8_bit_1_out_4), .in1(register_8_bit_5_out_4), .in2(register_8_bit_9_out_4),
    .in3(register_8_bit_13_out_4), .in4(register_8_bit_2_out_4), .in5(register_8_bit_6_out_4),
    .in6(register_8_bit_10_out_4), .in7(register_8_bit_14_out_4), .in8(register_8_bit_3_out_4),
    .in9(register_8_bit_7_out_4), .in10(register_8_bit_11_out_4), .in11(register_8_bit_15_out_4),
    .in12(register_8_bit_4_out_4), .in13(register_8_bit_8_out_4), .in14(register_8_bit_12_out_4),
    .in15(register_8_bit_16_out_4), .out(Data_out1), .sel(Out1_address));
  Multiplexer #(.select(4), .width(8)) multiplexer_2 (
    .in0(register_8_bit_1_out_4), .in1(register_8_bit_5_out_4), .in2(register_8_bit_9_out_4),
    .in3(register_8_bit_13_out_4), .in4(register_8_bit_2_out_4), .in5(register_8_bit_6_out_4),
    .in6(register_8_bit_10_out_4), .in7(register_8_bit_14_out_4), .in8(register_8_bit_3_out_4),
    .in9(register_8_bit_7_out_4), .in10(register_8_bit_11_out_4), .in11(register_8_bit_15_out_4),
    .in12(register_8_bit_4_out_4), .in13(register_8_bit_8_out_4), .in14(register_8_bit_12_out_4),
    .in15(register_8_bit_16_out_4), .out(Data_out2), .sel(Out2_address));
  Multiplexer #(.select(4), .width(8)) multiplexer_3 (
    .in0(register_8_bit_1_out_4), .in1(register_8_bit_5_out_4), .in2(register_8_bit_9_out_4),
    .in3(register_8_bit_13_out_4), .in4(register_8_bit_2_out_4), .in5(register_8_bit_6_out_4),
    .in6(register_8_bit_10_out_4), .in7(register_8_bit_14_out_4), .in8(register_8_bit_3_out_4),
    .in9(register_8_bit_7_out_4), .in10(register_8_bit_11_out_4), .in11(register_8_bit_15_out_4),
    .in12(register_8_bit_4_out_4), .in13(register_8_bit_8_out_4), .in14(register_8_bit_12_out_4),
    .in15(register_8_bit_16_out_4), .out(Data_out3), .sel(Out3_address));
endmodule

module Control_logic (
  input  [15:0] in_1,
  input  zero,
  input  negative,
  input  In_rd,
  input  [3:0] In_rd_data,
  input  In_rd_1,
  input  [3:0] In_rd_data_1,
  input  In_rd_2,
  input  [3:0] In_rd_data_2,
  input  [7:0] istr_addr_in,
  input  sf1,
  input  sf2,
  input  sf3,
  input  sf4,
  output [3:0] rd,
  output rd_en,
  output [3:0] rs1,
  output rs1_en,
  output [3:0] rs2,
  output rs2_en,
  output [7:0] im,
  output im_en,
  output Alu_en,
  output Alu_op,
  output Alu_rs1_im,
  output Jump,
  output [7:0] Istr_addr,
  output Block_fetch,
  output [3:0] rst,
  output rst_en,
  output load_en,
  output [2:0] rgb,
  output clr,
  output screen_en
);

  wire add, addi, and_1_out, and_2_out, and_3_out, and_6_out, and_8_out, and_9_out, and_10_out, and_11_out,
       and_12_out, and_13_out, and_14_out, and_15_out, and_16_out, and_17_out, and_18_out, and_19_out,
       and_20_out, and_21_out, and_22_out, and_23_out, and_26_out, and_27_out, and_28_out, and_30_out,
       and_31_out, and_32_out, and_33_out, and_34_out, and_38_out, and_40_out, and_41_out, and_42_out,
       and_43_out, and_44_out, and_45_out, and_46_out, and_47_out, and_48_out, demultiplexer_1_out4,
       demultiplexer_2_out0, demultiplexer_2_out1, demultiplexer_2_out2, demultiplexer_2_out3,
       demultiplexer_2_out4, demultiplexer_2_out5, demultiplexer_2_out6, demultiplexer_2_out7,
       demultiplexer_2_out8, demultiplexer_2_out9, demultiplexer_2_out10, gosub, load, loadi, not_1_out,
       not_2_out, not_3_out, or_6_out, or_7_out, or_8_out, or_9_out, or_10_out, or_13_out, retur, screen,
       str, stri;
  wire [2:2] demultiplexer_1_out11;
  wire [3:0] and_5_out, and_7_out, and_29_out, multiplexer_2_out, xor_1_out, xor_2_out, xor_3_out, xor_4_out,
       xor_5_out, xor_6_out, xor_7_out, xor_8_out, xor_9_out;
  wire [3:3] and_24_out, or_1_out, or_3_out, or_4_out;
  wire [7:0] and_37_out, bit_extender_1_out, multiplexer_1_out, return_addr, return_addr_q;
  wire [7:7] and_25_out;

  Demultiplexer #(.select(4)) demultiplexer_1 (
    .out1(add), .out2(Alu_op), .out3(addi), .out4(demultiplexer_1_out4), .out5(gosub), .out6(retur),
    .out7(loadi), .out8(load), .out9(stri), .out10(str), .out11(demultiplexer_1_out11[2]), .out12(screen),
    .in(1'b1), .sel(in_1[3:0]));  // open: out0, out13, out14, out15
  Demultiplexer #(.select(4)) demultiplexer_2 (
    .out0(demultiplexer_2_out0), .out1(demultiplexer_2_out1), .out2(demultiplexer_2_out2),
    .out3(demultiplexer_2_out3), .out4(demultiplexer_2_out4), .out5(demultiplexer_2_out5),
    .out6(demultiplexer_2_out6), .out7(demultiplexer_2_out7), .out8(demultiplexer_2_out8),
    .out9(demultiplexer_2_out9), .out10(demultiplexer_2_out10), .in(demultiplexer_1_out4), .sel(in_1[7:4]));  // open: out11, out12, out13, out14, out15
  or or_1 (or_1_out[3], add, Alu_op, addi, loadi, load, demultiplexer_1_out11[2]);
  or or_2 (rst_en, str, stri);
  or or_3 (or_3_out[3], add, Alu_op, addi, load, str);
  not not_1 (not_1_out, zero);
  not not_2 (not_2_out, negative);
  and and_1 (and_1_out, rs1_en, In_rd);
  and and_2 (and_2_out, rs1_en, In_rd_1);
  and and_3 (and_3_out, rs1_en, In_rd_2);
  assign rd = in_1[7:4] & {4{or_1_out[3]}};  // AND_Gate and_4, 4 bits wide
  assign and_5_out = {4{or_3_out[3]}} & in_1[11:8];  // AND_Gate and_5, 4 bits wide
  or or_4 (or_4_out[3], add, Alu_op);
  or or_5 (load_en, load, loadi);
  and and_6 (and_6_out, not_1_out, not_2_out);
  assign xor_1_out = ~rs1 ^ In_rd_data;  // XOR_Gate xor_1, 4 bits wide
  assign xor_2_out = ~rs1 ^ In_rd_data_1;  // XOR_Gate xor_2, 4 bits wide
  assign xor_3_out = ~rs1 ^ In_rd_data_2;  // XOR_Gate xor_3, 4 bits wide
  or or_6 (or_6_out, or_3_out[3], loadi, stri, demultiplexer_1_out11[2]);
  assign and_7_out = {4{or_4_out[3]}} & in_1[15:12];  // AND_Gate and_7, 4 bits wide
  Multiplexer #(.width(8)) multiplexer_1 (.in0(in_1[15:8]), .in1(in_1[11:4]), .out(multiplexer_1_out), .sel(gosub));
  and and_8 (and_8_out, and_1_out, and_9_out);
  and and_9 (and_9_out, xor_1_out[0], xor_1_out[1], xor_1_out[2], xor_1_out[3]);
  and and_10 (and_10_out, and_2_out, and_11_out);
  and and_11 (and_11_out, xor_2_out[0], xor_2_out[1], xor_2_out[2], xor_2_out[3]);
  and and_12 (and_12_out, and_3_out, and_13_out);
  and and_13 (and_13_out, xor_3_out[0], xor_3_out[1], xor_3_out[2], xor_3_out[3]);
  Multiplexer #(.width(4)) multiplexer_2 (.in0(and_5_out), .in1(4'b0000), .out(multiplexer_2_out), .sel(or_7_out));
  or or_7 (or_7_out, stri, demultiplexer_1_out11[2], loadi);
  or or_8 (or_8_out, addi, stri, loadi, load, demultiplexer_1_out11[2]);
  Multiplexer #(.width(8)) multiplexer_3 (.in0(multiplexer_1_out), .in1(return_addr), .out(Istr_addr), .sel(retur));
  or or_9 (or_9_out, zero, negative);
  Register u_return_addr (.D(istr_addr_in), .en(gosub), .clk(gosub), .Q(return_addr_q));  // open: clr
  Multiplexer #(.width(4)) multiplexer_4 (.in0(multiplexer_2_out), .in1(in_1[7:4]), .out(rs1), .sel(screen));
  Multiplexer #(.width(4)) multiplexer_5 (.in0(and_7_out), .in1(in_1[11:8]), .out(rs2), .sel(screen));
  or or_10 (or_10_out, or_8_out, str);
  not not_3 (not_3_out, or_3_out[3]);
  and and_14 (and_14_out, demultiplexer_2_out7, sf1);
  and and_15 (and_15_out, demultiplexer_2_out8, sf2);
  and and_16 (and_16_out, demultiplexer_2_out9, sf3);
  and and_17 (and_17_out, demultiplexer_2_out10, sf4);
  and and_18 (and_18_out, demultiplexer_2_out1, zero);
  and and_19 (and_19_out, demultiplexer_2_out2, negative);
  and and_20 (and_20_out, demultiplexer_2_out3, and_6_out);
  and and_21 (and_21_out, demultiplexer_2_out4, not_1_out);
  and and_22 (and_22_out, demultiplexer_2_out5, not_2_out);
  and and_23 (and_23_out, demultiplexer_2_out6, or_9_out);
  and and_24 (and_24_out[3], or_3_out[3], or_10_out);
  and and_25 (and_25_out[7], not_3_out, or_8_out);
  and and_26 (and_26_out, rs2_en, In_rd);
  and and_27 (and_27_out, rs2_en, In_rd_1);
  and and_28 (and_28_out, rs2_en, In_rd_2);
  Adder_8_Bit adder_8_bit_1 (.A(return_addr_q), .B({8{1'b0}}), .r(1'b1), .Somma(return_addr));  // open: Resto
  or or_11 (rs2_en, or_4_out[3], screen);
  assign xor_4_out = ~rs2 ^ In_rd_data;  // XOR_Gate xor_4, 4 bits wide
  assign xor_5_out = ~rs2 ^ In_rd_data_1;  // XOR_Gate xor_5, 4 bits wide
  assign xor_6_out = ~rs2 ^ In_rd_data_2;  // XOR_Gate xor_6, 4 bits wide
  or or_12 (rs1_en, or_6_out, screen);
  assign and_29_out = {4{and_24_out[3]}} & in_1[15:12];  // AND_Gate and_29, 4 bits wide
  or or_13 (or_13_out, and_14_out, and_15_out, and_16_out, and_17_out, demultiplexer_2_out0, and_18_out, and_19_out, and_20_out, and_21_out, and_22_out, and_23_out);
  and and_30 (and_30_out, xor_4_out[0], xor_4_out[1], xor_4_out[2], xor_4_out[3]);
  and and_31 (and_31_out, and_27_out, and_32_out);
  and and_32 (and_32_out, xor_5_out[0], xor_5_out[1], xor_5_out[2], xor_5_out[3]);
  and and_33 (and_33_out, and_28_out, and_34_out);
  and and_34 (and_34_out, xor_6_out[0], xor_6_out[1], xor_6_out[2], xor_6_out[3]);
  and and_35 (clr, in_1[15], screen);
  and and_36 (screen_en, screen, ~Block_fetch);  // AND_Gate
  assign and_37_out = {8{and_25_out[7]}} & in_1[15:8];  // AND_Gate and_37, 8 bits wide
  or or_14 (Alu_en, str, stri, add, load_en, Alu_op, addi, demultiplexer_1_out11[2]);
  or or_15 (Alu_rs1_im, demultiplexer_1_out11[2], addi, load_en, rst_en);
  or or_16 (Jump, gosub, retur, or_13_out);
  and and_38 (and_38_out, and_26_out, and_30_out);
  and and_39 (rd_en, ~Block_fetch, or_1_out[3]);  // AND_Gate
  assign bit_extender_1_out = {{4{and_29_out[3]}}, and_29_out};  // Bit_Extender bit_extender_1
  and and_40 (and_40_out, rst_en, In_rd);
  and and_41 (and_41_out, rst_en, In_rd_1);
  and and_42 (and_42_out, rst_en, In_rd_2);
  assign im = bit_extender_1_out | and_37_out;  // OR_Gate or_17, 8 bits wide
  or or_18 (im_en, and_25_out[7], and_24_out[3]);
  assign xor_7_out = ~in_1[7:4] ^ In_rd_data;  // XOR_Gate xor_7, 4 bits wide
  assign xor_8_out = ~in_1[7:4] ^ In_rd_data_1;  // XOR_Gate xor_8, 4 bits wide
  assign xor_9_out = ~in_1[7:4] ^ In_rd_data_2;  // XOR_Gate xor_9, 4 bits wide
  and and_43 (and_43_out, xor_7_out[0], xor_7_out[1], xor_7_out[2], xor_7_out[3]);
  and and_44 (and_44_out, xor_8_out[0], xor_8_out[1], xor_8_out[2], xor_8_out[3]);
  and and_45 (and_45_out, xor_9_out[0], xor_9_out[1], xor_9_out[2], xor_9_out[3]);
  and and_46 (and_46_out, and_40_out, and_43_out);
  and and_47 (and_47_out, and_41_out, and_44_out);
  and and_48 (and_48_out, and_42_out, and_45_out);
  or or_19 (Block_fetch, and_8_out, and_38_out, and_46_out, and_10_out, and_31_out, and_47_out, and_12_out, and_33_out, and_48_out);

  assign rgb = in_1[14:12];
  assign rst = in_1[7:4];

  // Other names for the same wires on the sheet: sub = Alu_op; last4bit[3:0] = in_1[15:12]
endmodule
